# Fritzing sketch FlightController (saved by Fritzing 0.9.2b)
circuit board: 1.76294cm x 2.344cm
circuit board: 10.0204cm x 7.8729cm
breadboards: 1

parts:
  U1 = atmega168 [package=dip]
  XTAL1 = Crystal [frequency="16 Mhz" package=THT]
  U2 = Voltage Regulator - 5V [package="TO220 [THT]"]
  R1 = Resistor [tolerance=±5% resistance=220 package=THT]
  R2 = Resistor [tolerance=±5% resistance=110k package=THT]
  C1 = Electrolytic Capacitor [capacitance=10µF package="100 mil [THT, electrolytic]"]
  C2 = Electrolytic Capacitor [capacitance=10µF package="100 mil [THT, electrolytic]"]
  C3 = Ceramic Capacitor [capacitance=22pF package="100 mil [THT, multilayer]"]
  C4 = Ceramic Capacitor [capacitance=22pF package="100 mil [THT, multilayer]"]
  LED1 = LED - 5mm [color="Red (633nm)" package="5 mm [THT]"]
  C5 = Ceramic Capacitor [capacitance=1µF package="100 mil [THT, multilayer]"]
  C6 = Ceramic Capacitor [capacitance=1µF package="100 mil [THT, multilayer]"]
  D1 = Rectifier Diode [part_number=1N4001 package="300 mil [THT]"]
  ESC_2 = longpad pin header, 3 pins [form="long pad"]
  VCC = Battery block 9V
  ESC1 = longpad pin header, 3 pins [form="long pad"]
  ESC_3 = longpad pin header, 3 pins [form="long pad"]
  J4 = longpad pin header, 3 pins [form="long pad"]
  S2 = SWITCH-MOMENTARY-2 [package=tactile-switch-1101ne]
  IMU = Generic male header - 8 pins [form="♂ (male)" package=THT]
  xBee = Generic male header - 6 pins [form="♂ (male)" package=THT]
  J5 = Generic double row male header - 40 pins [form="♂ (male)" package=THT]

nets:
  N1: U1.RESET, R2.Pin_0, S2.1
  N2: U1.D3_(PWM), ESC1.pin2
  5V: U1.VCC, U1.AVCC, U1.AREF, U2.output_voltage, R1.Pin_0, R2.Pin_1, C2.+, C5.1, ESC_2.pin3, ESC1.pin3, ESC_3.pin1, J4.pin1, IMU.VCC_IN, xBee.5V, J5.5V
  GND: U1.GND, U2.GND, C3.0, C4.0, ESC_2.pin1, VCC.+, ESC1.pin1, ESC_3.pin3, J4.pin3, S2.2, IMU.GND, xBee.GND, J5.GND
  N3: U1.XLAT1, XTAL1.pin_0, C3.1
  N4: U1.XLAT2, XTAL1.pin_1, C4.1
  N5: U1.D5_(PWM), ESC_2.pin2
  N6: U1.D6_(PWM), ESC_3.pin2
  N7: U1.D9_(PWM), J4.pin2
  N8: U1.D10_(PWM), J5.GPIO08
  N9: U1.D11_(PWM), J5.GPIO10
  N10: U1.D12, J5.GPIO09
  N11: U1.D13, J5.GPIO11
  N12: U1.A4, IMU.SDA
  N13: U1.A5, IMU.SCL
  N14: U2.input_voltage, C1.+, C6.1, D1.cathode
  N15: R1.Pin_1, LED1.anode
  N16: C1.-, C2.-, LED1.cathode, C5.0, C6.0
  N17: D1.anode, VCC.-
  N18: xBee.DOUT, J5.GPIO15
  N19: xBee.DIN, J5.GPIO14

notes:
  MOSI

custom parts:
  Generic male header - 8 pins: Generic male header
  Generic male header - 6 pins: Generic male header
  Generic double row male header - 40 pins: Generic double row male header
